# Fritzing sketch Casa Inteligente V2 (saved by Fritzing 0.9.10b)
breadboards: 1

parts:
  Componente1 = Arduino Uno (Rev3)
  LED1 = LED - 5mm [color="Red (633nm)" current=0.030 package="5 mm [THT]"]
  R1 = Resistor [tolerance=±5% power=0.25 resistance=13k package=THT]
  S1 = Toggle Switch [package=THT]
  S2 = Toggle Switch [package=THT]
  LED2 = LED - 5mm [color="Red (633nm)" current=0.030 package="5 mm [THT]"]
  R2 = Resistor [tolerance=±5% power=0.25 resistance=13k package=THT]
  S3 = Toggle Switch [package=THT]
  R3 = Photocell (LDR) [package=THT]
  R4 = Resistor [tolerance=±5% power=0.25 resistance=31 package=THT]
  R5 = Resistor [tolerance=±5% power=0.25 resistance=13k package=THT]
  R6 = Resistor [tolerance=±5% power=0.25 resistance=13k package=THT]
  LED3 = LED - 5mm [color="Red (633nm)" current=0.030 package="5 mm [THT]"]
  LED4 = LED - 5mm [color="Red (633nm)" current=0.030 package="5 mm [THT]"]
  LED5 = LED - 5mm [color="Red (633nm)" current=0.030 package="5 mm [THT]"]
  LED6 = LED - 5mm [color="Red (633nm)" current=0.030 package="5 mm [THT]"]
  R7 = Resistor [tolerance=±5% power=0.25 resistance=13k package=THT]
  R8 = Resistor [tolerance=±5% power=0.25 resistance=13k package=THT]
  S4 = Pushbutton [package="[THT]"]
  LED7 = LED - 5mm [color="Red (633nm)" current=0.030 package="5 mm [THT]"]
  LED8 = LED - 5mm [color="Red (633nm)" current=0.030 package="5 mm [THT]"]
  R9 = Resistor [tolerance=±5% power=0.25 resistance=13k package=THT]
  R10 = Resistor [tolerance=±5% power=0.25 resistance=13k package=THT]
  J1 = Basic Servo
  Componente2 = Bluetooth HC-05 Macho
  R11 = Resistor [tolerance=±5% power=0.25 resistance=2.2k package=THT]
  R12 = Resistor [tolerance=±5% power=0.25 resistance=1k package=THT]
  J2 = Piezo Speaker
  J3 = Piezo Speaker
  R13 = Resistor [tolerance=±5% power=0.25 resistance=100 package=THT]
  R14 = Resistor [tolerance=±5% power=0.25 resistance=100 package=THT]

nets:
  N1: Componente1.A0, R3.pin_0, R4.Pin_1
  N2: Componente1.D8, LED7.cathode
  N3: Componente1.D9_PWM, J1.pulse
  N4: Componente1.D10_PWM/SS, S3.COM
  N5: Componente1.D11_PWM/MOSI, S2.COM
  N6: Componente1.D12/MISO, R14.Pin_0
  N7: Componente1.D13/SCK, R13.Pin_0
  N8: Componente1.D0/RX, Componente2.TXD
  N9: Componente1.D1/TX, R12.Pin_0
  N10: Componente1.D2, S4.Pin_1, S4.Pin_2
  N11: Componente1.D3_PWM, LED3.cathode
  N12: Componente1.D4, LED5.cathode
  N13: Componente1.D5_PWM, LED6.cathode
  N14: Componente1.D6_PWM, LED4.cathode
  N15: Componente1.D7, LED8.cathode
  VCC: Componente1.5V, J1.vcc, Componente2.VCC
  GND: Componente1.GND, LED1.cathode, LED2.cathode, R4.Pin_0, R5.Pin_1, R6.Pin_1, R7.Pin_1, R8.Pin_1, S4.Pin_3, S4.Pin_4, R9.Pin_1, R10.Pin_1, J1.gnd, Componente2.GND, R11.Pin_0, J2.pin1, J3.pin1
  N16: LED1.anode, R1.Pin_0
  N17: R1.Pin_1, S1.COM
  N18: S1.L1, S2.L1
  N19: S1.L2, S2.L2
  N20: LED2.anode, R2.Pin_0
  N21: R2.Pin_1, S3.L1
  N22: R5.Pin_0, LED5.anode
  N23: R6.Pin_0, LED3.anode
  N24: LED4.anode, R8.Pin_0
  N25: LED6.anode, R7.Pin_0
  N26: LED7.anode, R9.Pin_0
  N27: LED8.anode, R10.Pin_0
  N28: Componente2.RXD, R11.Pin_1, R12.Pin_1
  N29: J2.pin2, R13.Pin_1
  N30: J3.pin2, R14.Pin_1
